// Logisim project GuessTheNumber.circ as structural Verilog
module main (
  input  in_1,
  input  in_2,
  input  in_3,
  input  in_4,
  input  in_5,
  input  in_6,
  input  in_7,
  input  in_8
);
endmodule

module game (
  input  Jogar,
  input  A,
  input  B,
  input  Jogador,
  output maior,
  output out_6,
  output igual,
  output menor
);

  mux mux_1 (.A(A), .B(B), .S(Jogador), .C(out_6));
  comparador comparador ();
  // AND_Gate and_1 is placed but not wired
  // AND_Gate and_2 is placed but not wired
  // AND_Gate and_3 is placed but not wired
endmodule

module mux (
  input  A,
  input  B,
  input  S,
  output C
);

  wire and_1_out, and_2_out, not_1_out;

  not not_1 (not_1_out, S);
  and and_1 (and_1_out, not_1_out, A);
  and and_2 (and_2_out, S, B);
  or or_1 (C, and_1_out, and_2_out);
endmodule

module mux_2x1__4_bits (
  input  S,
  input  A0,
  input  B0,
  input  A1,
  input  B1,
  input  A2,
  input  B2,
  input  A3,
  input  B3,
  output C0,
  output C1,
  output C2,
  output C3
);

  mux mux_1 (.A(A0), .B(B0), .S(S), .C(C0));
  mux mux_2 (.A(A1), .B(B1), .S(S), .C(C1));
  mux mux_3 (.A(A2), .B(B2), .S(S), .C(C2));
  mux mux_4 (.A(A3), .B(B3), .S(S), .C(C3));
endmodule
